// Logisim project 4_aba_aois_2.circ as structural Verilog: 1 circuit, main circuit main
module main (
  input  X1,
  input  X2,
  input  X3,
  input  X4,
  output out_5,
  output out_6,
  output out_7,
  output out_8
);

  wire and_1_out, and_2_out, and_3_out, and_4_out, and_5_out, and_6_out, and_7_out, and_8_out, and_9_out,
       and_10_out, not_1_out, not_2_out, not_3_out, not_4_out;

  not not_1 (not_1_out, X1);
  not not_2 (not_2_out, X2);
  not not_3 (not_3_out, X3);
  not not_4 (not_4_out, X4);
  and and_1 (and_1_out, X1, X2, X3);
  and and_2 (and_2_out, X1, X2, not_3_out);
  and and_3 (and_3_out, X3, not_2_out);
  and and_4 (and_4_out, X3, not_1_out);
  and and_5 (and_5_out, X4, X2);
  and and_6 (and_6_out, not_4_out, X2, not_1_out);
  and and_7 (and_7_out, not_4_out, not_2_out, X1);
  and and_8 (and_8_out, not_3_out, not_2_out, X1);
  and and_9 (and_9_out, X4, X2);
  and and_10 (and_10_out, X4, X3);
  or or_1 (out_5, and_1_out, X4);
  or or_2 (out_6, and_2_out, and_3_out, and_4_out, and_5_out);
  or or_3 (out_7, and_6_out, and_7_out, and_8_out);
  or or_4 (out_8, not_1_out, and_9_out, and_10_out);

  // Notes on the sheet:
  //   X1
  //   X2
  //   X3
  //   X4
  //   !X3
  //   !X1
  //   !X4
  //   !X2
endmodule
