// Logisim project 4_laba_aois.circ as structural Verilog: 2 circuits, main circuit main
module main (
  input  x1,
  input  x2,
  input  x3,
  output B,
  output D
);

  wire and_1_out, and_2_out, and_3_out, and_4_out, and_5_out, not_1_out, not_2_out, not_3_out, xor_1_out;

  not not_1 (not_1_out, x1);
  not not_2 (not_2_out, x2);
  not not_3 (not_3_out, x3);
  and and_1 (and_1_out, not_1_out, x2);
  and and_2 (and_2_out, not_1_out, x3);
  and and_3 (and_3_out, x2, x3);
  and and_4 (and_4_out, not_1_out, x2, x3);
  or or_1 (B, and_1_out, and_2_out, and_3_out);
  and and_5 (and_5_out, x1, not_2_out, not_3_out);
  xor xor_1 (xor_1_out, B, and_4_out);
  or or_2 (D, xor_1_out, and_5_out);

  // Notes on the sheet:
  //   X1
  //   X3
  //   X2
  //   !X2
  //   !X3
  //   !X1
endmodule

module main_f (
  input  [7:0] in_1,
  input  [7:0] in_2,
  output [7:0] out_3
);

  wire main_1_b, main_2_b, main_3_b, main_4_b, main_5_b, main_6_b, main_7_b, main_8_b;

  // Probe on in_1
  // Probe on in_2
  main main_1 (.x1(in_1[0]), .x2(in_2[0]), .x3(main_8_b), .B(main_1_b), .D(out_3[0]));
  main main_2 (.x1(in_1[1]), .x2(in_2[1]), .x3(main_1_b), .B(main_2_b), .D(out_3[1]));
  main main_3 (.x1(in_1[2]), .x2(in_2[2]), .x3(main_2_b), .B(main_3_b), .D(out_3[2]));
  main main_4 (.x1(in_1[3]), .x2(in_2[3]), .x3(main_3_b), .B(main_4_b), .D(out_3[3]));
  main main_5 (.x1(in_1[4]), .x2(in_2[4]), .x3(main_4_b), .B(main_5_b), .D(out_3[4]));
  main main_6 (.x1(in_1[5]), .x2(in_2[5]), .x3(main_5_b), .B(main_6_b), .D(out_3[5]));
  main main_7 (.x1(in_1[6]), .x2(in_2[6]), .x3(main_6_b), .B(main_7_b), .D(out_3[6]));
  main main_8 (.x1(in_1[7]), .x2(in_2[7]), .x3(main_7_b), .B(main_8_b), .D(out_3[7]));
  // Probe on out_3
endmodule
